# Fritzing sketch esp32_SMART_HOME (saved by Fritzing 0.9.3b)
breadboards: 1

parts:
  U1 = ESP32S-HiLetgo [part_number=ESP32S-HiLetgo]
  DHT1 = Humidity and Temperature Sensor DHT11
  Relay_5V1 = Keyes Relay [package=THT]
  S1 = KY-026
  Componente5 = MQ-131 breakout
  R1 = Resistor [tolerance=±5% resistance=10k package=THT]
  R2 = Resistor [tolerance=±5% resistance=10k package=THT]
  R3 = Resistor [tolerance=±5% resistance=10k package=THT]

nets:
  N1: U1.3.3, DHT1.Vcc, Relay_5V1.power, R2.Pin_1
  N2: U1.GPIO35, S1.pin1, R1.Pin_0
  N3: U1.GPIO32, Componente5.VCC, R3.Pin_0
  N4: U1.VIN, S1.pin3, Componente5.AO, R1.Pin_1, R3.Pin_1
  N5: U1.GPIO0, Relay_5V1.signal
  GND: U1.GND, DHT1.GND_1, Relay_5V1.ground, S1.pin2, Componente5.GND
  N6: U1.GPIO22, DHT1.Data-signal, R2.Pin_0

notes:
  MQ-2

custom parts:
  ESP32S-HiLetgo: HiLetgo ESP-WROOM-32 ESP32 ESP-32S Development Board 2.4GHz Dual-Mode WiFi + Bluetooth Dual Cores Microcontroller The ESP32 integrated with Antenna switches, RF Balun, power amplifiers, low-noise amplifiers, filters, and management modules, and the entire solution occupies the least area of PCB. 2.4 GHz Wi-Fi plus Bluetooth dual-mode chip, with TSMC Ultra-low power consumption 40nm technology,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
  Humidity and Temperature Sensor DHT11: Digital relative humidity & temperature sensor DHT11
  Keyes Relay: The Keyes 5V relay module is suitable for SCM development, home appliance control. It uses a 5V~12V TIL control signal which can control DC / AC signal.
  KY-026: ky-026 flame sensor module
  MQ-131 breakout: SKU: 101282
